# Fritzing sketch solenoid_driver (saved by Fritzing 0.9.9b)
breadboards: 1

parts:
  L1 = Solenoid
  D1 = Diode [package=diode-1n4148]
  Q1 = npn-Powertransistor [package="TO220 [THT]"]
  R1 = Resistor [tolerance=±5% power=0.25 resistance=220 package=THT]

nets:
  N1: L1.pin1, D1.A, Q1.collector
  N2: Q1.emitter, R1.Pin_0
